# Fritzing sketch led (saved by Fritzing 0.8.7b)
breadboards: 1

parts:
  LED1 = LED - 5mm [color="Red (633nm)" package="5 mm [THT]"]
  R1 = Resistor [tolerance=±5% resistance=330 package=THT]

nets:
  N1: LED1.anode, R1.Pin_0

notes:
  GND
  GPIO
